// Logisim project ArquivoFinalizado.circ as structural Verilog: 26 circuits, main circuit OF - Cronometro
module OF___GAME_FINALIZADO (
  input  in_1,
  input  in_2,
  input  in_3,
  input  in_4,
  input  in_5,
  input  in_6,
  input  in_7,
  input  in_8
);

  wire A, A_0, A_JOGANDO, A_VENCEU, ACERTOU, ALL, and_2_out, and_3_out, and_4_out, and_14_out, and_17_out,
       and_18_out, and_19_out, and_20_out, and_21_out, and_22_out, and_24_out, and_25_out, and_26_out,
       and_27_out, and_28_out, and_29_out, AON, APENASA, APENASB, B, B_0, B_JOGANDO, B_VENCEU, BON,
       CHUTANDO_X, CHUTANDO_Y, CHUTAR, clock_1_out, clock_2_out, CONFIGURAR, CsGx, CsGy, d_ff_1_q, d_ff_3_q,
       dma_t, dmb_t, dna_1, dnb_1, DRAW, dsa_t, dsb_t, END_GAME, FF, IGUAL, MAIOR, MENOR, not_1_out,
       not_2_out, not_3_out, not_4_out, not_5_out, not_6_out, not_7_out, not_8_out, not_9_out, not_10_out,
       not_11_out, not_12_out, not_13_out, not_14_out, of_comparador_1_a__random___maior_que_b__meu,
       of_comparador_1_a__random___menor_que_b__meu, of_comparador_1_igual, of_comparador_soma_1_out_7,
       of_comparador_soma_1_out_10, of_hab_desab_chutes_1_sa, of_hab_desab_chutes_1_sa_2,
       of_hab_desab_chutes_1_sb, of_hab_desab_chutes_1_sb_2, or_1_out, or_2_out, or_3_out, or_4_out,
       or_5_out, or_6_out, or_7_out, or_8_out, or_9_out, or_10_out, or_12_out, or_13_out, or_15_out,
       or_17_out, or_18_out, or_22_out, or_23_out, or_24_out, or_27_out, or_28_out, or_29_out, or_30_out,
       or_31_out, or_34_out, or_35_out, or_40_out, or_42_out, or_43_out, or_44_out, or_45_out, or_46_out,
       or_47_out, or_48_out, or_49_out, or_50_out, or_51_out, or_52_out, or_56_out, or_57_out, or_58_out,
       or_63_out, or_64_out, P1, P1a, P1b, P2, P2a, P2b, P3, P3a, P3b, P4, P4a, P4b, P5, P5a, P5b, P6, P6a,
       P6b, P7, P7a, P7b, P8, P8a, P8b, P9, P9a, P9b, Pa_15, Pa_16, Pb_15, Pb_16, Pd, Pd1, Pd2, Pl2a, Pl2b,
       \PRÓXIMO , QA, QB, ran_SINAL_SOMA, rCSS, register_1_q, register_2_q, register_8_q, register_10_q,
       RESET, SA, SB, sGx, sGy, SHOW, SINAL_SOMA, START, SX, SY, tunnel, uma_t, umb_t, una_5, una_6, unb_5,
       unb_6, undriven, usa_t, usb_t;
  wire [3:0] \a_saída_p__display , \b_saída_p__display , CrGx, CrGy, crx, cry, DISPLAY_CM_SOMA,
       DISPLAY_CM_SOMA_t, DMA, DMB, DSA, DSB, GA, GB, of_comparador_soma_1_out_8,
       of_comparador_soma_1_out_11, PA, PAB, PB, PBB, ran_DISPLAY_CM_SOMA, rCDS, rGx, rGy, rx, ry, UMA, UMB,
       USA, USB, XH, XHDesfeito, YH, YHDesfeito;

  Button button_1 (.out(dma_t));
  Hex_Digit_Display hex_digit_display_1 (.value(DMA));  // open: dp
  Hex_Digit_Display hex_digit_display_2 (.value(PAB));  // open: dp
  Hex_Digit_Display hex_digit_display_3 (.value(PA));  // open: dp
  Button button_2 (.out(uma_t));
  LED led_1 (.in(1'b1));
  LED led_2 (.in(1'b1));
  Hex_Digit_Display hex_digit_display_4 (.value(UMA));  // open: dp
  _7_Segment_Display u_7_segment_display_1 (.g(SA), .c(undriven), .dp(undriven));  // open: f, a, b, e, d
  LED led_3 (.in(A_JOGANDO));
  Hex_Digit_Display hex_digit_display_5 (.value(crx));  // open: dp
  Hex_Digit_Display hex_digit_display_6 (.value(cry));  // open: dp
  \OF___Botão_para_próximo_ou_chute  \of_botão_para_próximo_ou_chute_1  (
    .CHUTE(CHUTAR), .\PRÓXIMO (\PRÓXIMO ), .START(START), .RESET(or_4_out), .HABILITA_AX(P1a),
    .CHUTA_AX(P2a), .HABILITA_AY(P3a), .CHUTA_AY(P4a), .COMPARA(P5a), .HABILITA_BX(P6a), .HABILITA_BY(P8a),
    .CHUTA_BY(P9a), .COMPARA_2(Pd1), .CHUTA_BX(P7a));
  and and_1 (APENASB, A_0, B_JOGANDO);
  _7_Segment_Display u_7_segment_display_2 (.g(of_comparador_soma_1_out_7));  // open: f, a, b, e, d, c, dp
  and and_2 (and_2_out, ACERTOU, P5);
  or or_1 (or_1_out, RESET, START);
  Button button_3 (.out(dsa_t));
  Button button_4 (.out(usa_t));
  Hex_Digit_Display hex_digit_display_7 (.value(DSA));  // open: dp
  Hex_Digit_Display hex_digit_display_8 (.value(USA));  // open: dp
  Hex_Digit_Display hex_digit_display_9 (.value(GA));  // open: dp
  Register #(.width(1), .Select("low")) register_1 (
    .D(1'b1), .Q(register_1_q), .clk(A_JOGANDO), .clr(or_2_out));  // open: en
  or or_2 (or_2_out, B_JOGANDO, CONFIGURAR, A_0);
  D_Flip_Flop d_ff_1 (.Q(d_ff_1_q), .preset(START), .reset(or_3_out));  // open: clk, D, Qn
  or or_3 (or_3_out, RESET, CONFIGURAR);
  or or_4 (or_4_out, CONFIGURAR, or_10_out);
  Hex_Digit_Display hex_digit_display_10 (.value(of_comparador_soma_1_out_8));  // open: dp
  or or_5 (or_5_out, Pd, P5);
  OF___Placar_para_unidades of_placar_para_unidades_1 (
    .Botton(and_2_out), .\SAÍDA_P__DISPLAY (PA), .PLACAR2(Pl2a), .RESET(or_6_out));
  or or_6 (or_6_out, RESET, B_VENCEU, Pa_16);
  OF___Placar_para_dezenas of_placar_para_dezenas_1 (.Botton(Pl2a), .\SAÍDA_P__DISPLAY (PAB), .RESET(or_7_out));
  or or_7 (or_7_out, RESET, B_VENCEU, Pa_16);
  and and_3 (and_3_out, ACERTOU, Pd);
  OF___Placar_para_unidades of_placar_para_unidades_2 (
    .Botton(and_3_out), .\SAÍDA_P__DISPLAY (PB), .PLACAR2(Pl2b), .RESET(or_8_out));
  or or_8 (or_8_out, RESET, Pa_16, Pb_16);
  OF___Placar_para_dezenas of_placar_para_dezenas_2 (.Botton(Pl2b), .\SAÍDA_P__DISPLAY (PBB), .RESET(or_9_out));
  or or_9 (or_9_out, RESET, Pa_16, Pb_16);
  OF___FlipFlop_D_pessoal of_flipflop_d_pessoal_1 (.F1(CONFIGURAR), .F0(or_1_out), .Q(tunnel));  // open: nda
  LED led_4 (.in(A_VENCEU));
  Button button_5 (.out(START));
  LED led_5 (.in(MAIOR));
  Button button_6 (.out(\PRÓXIMO ));
  _7_Segment_Display u_7_segment_display_3 (.g(SX));  // open: f, a, b, e, d, c, dp
  Hex_Digit_Display hex_digit_display_11 (.value(XH));  // open: dp
  LED led_6 (.in(CHUTANDO_X));
  _7_Segment_Display u_7_segment_display_4 (.g(sGx));  // open: f, a, b, e, d, c, dp
  and and_4 (and_4_out, B_0, d_ff_1_q);
  or or_10 (or_10_out, RESET, APENASA, APENASB);
  \OF___Botão_para_casos_individuais  \of_botão_para_casos_individuais_1  (
    .CHUTE(CHUTAR), .\PRÓXIMO (\PRÓXIMO ), .START(QB), .RESET(or_13_out), .HABILITA_AX(P6b), .CHUTA_X(P7b),
    .HABILITA_Y(P8b), .CHUTA_Y(P9b), .COMPARA(Pd2));
  and and_5 (APENASA, B_0, A_JOGANDO);
  _7_Segment_Display u_7_segment_display_5 (.g(of_comparador_soma_1_out_10));  // open: f, a, b, e, d, c, dp
  Hex_Digit_Display hex_digit_display_12 (.value(of_comparador_soma_1_out_11));  // open: dp
  OF___Comparador_soma of_comparador_soma_1 (
    .RAND_SOMA(ran_DISPLAY_CM_SOMA), .IGUAL(IGUAL), .A___B___RANDOM___MEU_2(MAIOR),
    .A___B___RANDOM___MEU(MENOR), .out_7(of_comparador_soma_1_out_7), .out_8(of_comparador_soma_1_out_8),
    .out_10(of_comparador_soma_1_out_10), .out_11(of_comparador_soma_1_out_11), .sinal_soma(SINAL_SOMA),
    .rSS(ran_SINAL_SOMA), .CHUTE(or_5_out), .START(FF), .DISPLAY_COM_SOMA(DISPLAY_CM_SOMA));
  or or_11 (ALL, RESET, START, CONFIGURAR, \PRÓXIMO , CHUTAR);
  LED led_7 (.in(END_GAME));
  LED led_8 (.in(DRAW));
  LED led_9 (.in(tunnel));
  Button button_7 (.out(CONFIGURAR));
  LED led_10 (.in(ACERTOU));
  LED led_11 (.in(IGUAL));
  _7_Segment_Display u_7_segment_display_6 (.g(sGy));  // open: f, a, b, e, d, c, dp
  Hex_Digit_Display hex_digit_display_13 (.value(rGx));  // open: dp
  _7_Segment_Display u_7_segment_display_7 (.g(rCSS));  // open: f, a, b, e, d, c, dp
  Hex_Digit_Display hex_digit_display_14 (.value(rCDS));  // open: dp
  or or_12 (or_12_out, A, B);
  or or_13 (or_13_out, RESET, APENASA, CONFIGURAR, or_12_out);
  not not_1 (not_1_out, PAB[1]);
  and and_6 (dna_1, PAB[0], not_1_out, not_2_out, not_3_out);
  not not_2 (not_2_out, PAB[2]);
  not not_3 (not_3_out, PAB[3]);
  not not_4 (not_4_out, PBB[1]);
  not not_5 (not_5_out, PBB[2]);
  not not_6 (not_6_out, PBB[3]);
  and and_7 (Pa_16, una_6, dna_1);
  and and_8 (Pa_15, una_5, dna_1);
  and and_9 (Pb_16, unb_6, dnb_1);
  and and_10 (Pb_15, unb_5, dnb_1);
  LED led_12 (.in(B_VENCEU));
  Button button_8 (.out(RESET));
  LED led_13 (.in(MENOR));
  Button button_9 (.out(CHUTAR));
  _7_Segment_Display u_7_segment_display_8 (.g(SY));  // open: f, a, b, e, d, c, dp
  Hex_Digit_Display hex_digit_display_15 (.value(YH));  // open: dp
  LED led_14 (.in(CHUTANDO_Y));
  Hex_Digit_Display hex_digit_display_16 (.value(rGy));  // open: dp
  or or_14 (AON, START, register_1_q, and_4_out);
  or or_15 (or_15_out, CONFIGURAR, BON);
  or or_16 (B, P9a, P8a, P7a, P6a);
  and and_11 (dnb_1, PBB[0], not_4_out, not_5_out, not_6_out);
  Button button_10 (.out(dmb_t));
  Hex_Digit_Display hex_digit_display_17 (.value(DMB));  // open: dp
  or or_17 (or_17_out, dma_t, dmb_t);
  OF___Cronometro of_cronometro_1 (
    .START(AON), .CONFIGURAR(or_15_out), .RESET(RESET), .DM(or_17_out), .DM_2(DMA), .UM(or_18_out),
    .UM_2(UMA), .DS_2(DSA), .DS(or_24_out), .US_2(USA), .US(or_23_out), .CLK(clock_1_out), .ZERO(A_0));
  not not_7 (not_7_out, PA[0]);
  not not_8 (not_8_out, PA[3]);
  not not_9 (not_9_out, PB[0]);
  not not_10 (not_10_out, PB[3]);
  Hex_Digit_Display hex_digit_display_18 (.value(PBB));  // open: dp
  Hex_Digit_Display hex_digit_display_19 (.value(PB));  // open: dp
  Button button_11 (.out(umb_t));
  LED led_15 (.in(1'b1));
  LED led_16 (.in(1'b1));
  Hex_Digit_Display hex_digit_display_20 (.value(UMB));  // open: dp
  _7_Segment_Display u_7_segment_display_9 (.g(SB));  // open: f, a, b, e, d, c, dp
  LED led_17 (.in(B_JOGANDO));
  Hex_Digit_Display hex_digit_display_21 (.value(XHDesfeito));  // open: dp
  Hex_Digit_Display hex_digit_display_22 (.value(YHDesfeito));  // open: dp
  or or_18 (or_18_out, uma_t, umb_t);
  Clock clock_1 (.out(clock_1_out));
  or or_19 (A, P1a, P2a, P3a, P4a);
  or or_20 (P1, P1a, P1b);
  or or_21 (P6, P6a, P6b);
  or or_22 (or_22_out, Pd, P5);
  and and_12 (una_6, not_7_out, PA[1], PA[2], not_8_out);
  and and_13 (unb_6, not_9_out, PB[1], PB[2], not_10_out);
  and and_14 (and_14_out, ACERTOU, P5);
  Button button_12 (.out(dsb_t));
  Button button_13 (.out(usb_t));
  Hex_Digit_Display hex_digit_display_23 (.value(USB));  // open: dp
  Hex_Digit_Display hex_digit_display_24 (.value(DSB));  // open: dp
  Hex_Digit_Display hex_digit_display_25 (.value(GB));  // open: dp
  or or_23 (or_23_out, usa_t, usb_t);
  or or_24 (or_24_out, dsa_t, dsb_t);
  or or_25 (P2, P2a, P2b);
  or or_26 (P7, P7a, P7b);
  OF___Verificar_se_acertou of_verificar_se_acertou_1 (
    .\PRÓXIMO (\PRÓXIMO ), .RESET(RESET), .chute_x(XHDesfeito), .chute_y(YHDesfeito),
    .\PRÓXIMO_2 (\PRÓXIMO ), .RESET_2(RESET), .SAIDA_X(rx), .Acertou_3(ACERTOU), .SAIDA(ry),
    .CHUTE(or_22_out), .Acertou(ACERTOU), .Acertou_2(ACERTOU));
  not not_11 (not_11_out, PA[1]);
  not not_12 (not_12_out, PA[3]);
  OF___Incrementador_de_4_flipflops_normal u_a (
    .Botton(and_14_out), .RESET(or_27_out), .\SAÍDA_P__DISPLAY (\a_saída_p__display ));
  or or_27 (or_27_out, RESET, Pa_16, Pb_16);
  Register #(.width(1), .Select("low")) register_2 (
    .D(1'b1), .Q(register_2_q), .clk(B_JOGANDO), .clr(or_28_out));  // open: en
  or or_28 (or_28_out, A_JOGANDO, B_0, CONFIGURAR);
  \OF___Botão_para_casos_individuais  \of_botão_para_casos_individuais_2  (
    .CHUTE(CHUTAR), .\PRÓXIMO (\PRÓXIMO ), .START(QA), .RESET(or_31_out), .HABILITA_AX(P1b), .CHUTA_X(P2b),
    .HABILITA_Y(P3b), .CHUTA_Y(P4b), .COMPARA(P5b));
  Hex_Digit_Display hex_digit_display_26 (.value(rx));  // open: dp
  and and_15 (una_5, PA[0], not_11_out, PA[2], not_12_out);
  and and_16 (unb_5, PB[0], not_13_out, PB[2], not_14_out);
  not not_13 (not_13_out, PB[1]);
  not not_14 (not_14_out, PB[3]);
  or or_29 (or_29_out, RESET, CONFIGURAR);
  _7_Segment_Display u_7_segment_display_10 (.g(SINAL_SOMA));  // open: f, a, b, e, d, c, dp
  Hex_Digit_Display hex_digit_display_27 (.value(DISPLAY_CM_SOMA_t));  // open: dp
  or or_30 (or_30_out, A, B);
  or or_31 (or_31_out, RESET, APENASB, CONFIGURAR, or_30_out);
  or or_32 (P3, P3a, P3b);
  or or_33 (P8, P8a, P8b);
  Hex_Digit_Display hex_digit_display_28 (.value(ry));  // open: dp
  OF___Incrementador_de_4_flipflops_normal u_b (
    .Botton(and_17_out), .RESET(or_34_out), .\SAÍDA_P__DISPLAY (\b_saída_p__display ));
  and and_17 (and_17_out, ACERTOU, Pd);
  or or_34 (or_34_out, RESET, Pa_16, Pb_16);
  D_Flip_Flop d_ff_2 (.clk(FF), .Q(FF), .preset(START), .reset(or_29_out));  // open: D, Qn
  or or_35 (or_35_out, RESET, CONFIGURAR, B_0);
  or or_36 (P4, P4a, P4b);
  or or_37 (P9, P9a, P9b);
  LED led_18 (.in(MAIOR));
  Button button_14 (.out(SHOW));
  D_Flip_Flop d_ff_3 (.Q(d_ff_3_q), .preset(START), .reset(or_35_out));  // open: clk, D, Qn
  OF___Comparador of_comparador_1 (
    .Igual(of_comparador_1_igual),
    .A__random___MENOR_que_B__meu(of_comparador_1_a__random___menor_que_b__meu), .P(\b_saída_p__display ),
    .R(\a_saída_p__display ), .A__random___MAIOR_que_B__meu(of_comparador_1_a__random___maior_que_b__meu));
  LED led_19 (.in(IGUAL));
  and and_18 (and_18_out, A_0, d_ff_3_q);
  Counter #(.width(1), .max('h1)) counter_1 (
    .D(1'b1), .Q(QA), .clk(APENASA), .clr(P1b));  // open: load, count, carry, preset, down
  or or_38 (P5, P5a, P5b);
  or or_39 (Pd, Pd1, Pd2);
  and and_19 (and_19_out, B_0, FF, Pa_15);
  and and_20 (and_20_out, FF, A_0, Pb_15);
  or or_40 (or_40_out, Pa_15, Pb_15);
  and and_21 (and_21_out, B_0, A_0, FF);
  and and_22 (and_22_out, B_0, A_0);
  LED led_20 (.in(MENOR));
  or or_41 (BON, and_18_out, register_2_q);
  Counter #(.width(1), .max('h1)) counter_2 (
    .D(1'b1), .Q(QB), .clk(APENASB), .clr(P6b));  // open: load, count, carry, preset, down
  OF___Tabela_de_possibilidades_de_soma of_tabela_de_possibilidades_de_soma_1 (
    .DISPLAY_SOMA(DISPLAY_CM_SOMA_t), .SINAL_SOMA(SINAL_SOMA), .A(XHDesfeito), .B(YHDesfeito));
  OF___Tabela_de_possibilidades_de_soma of_tabela_de_possibilidades_de_soma_2 (
    .DISPLAY_SOMA(ran_DISPLAY_CM_SOMA), .SINAL_SOMA(ran_SINAL_SOMA), .A(rx), .B(ry));
  or or_42 (or_42_out, and_19_out, and_20_out);
  and and_23 (DRAW, FF, and_22_out, of_comparador_1_igual);
  and and_24 (and_24_out, END_GAME, of_comparador_1_a__random___maior_que_b__meu);
  and and_25 (and_25_out, of_comparador_1_a__random___menor_que_b__meu, END_GAME);
  OF___Cronometro of_cronometro_2 (
    .START(BON), .CONFIGURAR(or_44_out), .RESET(RESET), .DM(or_43_out), .DM_2(DMB), .UM(or_56_out),
    .UM_2(UMB), .DS_2(DSB), .DS(or_57_out), .US_2(USB), .US(or_58_out), .CLK(clock_2_out), .ZERO(B_0));
  or or_43 (or_43_out, dma_t, dmb_t);
  or or_44 (or_44_out, CONFIGURAR, AON);
  or or_45 (or_45_out, P1a, P1b);
  or or_46 (or_46_out, P2a, P2b);
  or or_47 (or_47_out, P3a, P3b);
  or or_48 (or_48_out, P4a, P4b);
  or or_49 (or_49_out, P6a, P6b);
  or or_50 (or_50_out, P7a, P7b);
  or or_51 (or_51_out, P8a, P8b);
  or or_52 (or_52_out, P9a, P9b);
  or or_53 (END_GAME, or_42_out, or_40_out, and_21_out);
  or or_54 (A_VENCEU, and_24_out, Pa_15);
  or or_55 (B_VENCEU, and_25_out, Pb_15);
  or or_56 (or_56_out, uma_t, umb_t);
  Clock clock_2 (.out(clock_2_out));
  or or_57 (or_57_out, dsa_t, dsb_t);
  or or_58 (or_58_out, usa_t, usb_t);
  OF___Hab_desab_chutes of_hab_desab_chutes_1 (
    .HABILITA_AX(or_45_out), .DESABILITA_CHUTA_AX(or_46_out), .HABILITA_BX(or_49_out),
    .DESABILITA_CHUTA_BX(or_50_out), .HABILITA__AY(or_47_out), .DESABILITA_CHUTA_AY(or_48_out),
    .HABILITA__BY(or_51_out), .DESABILITA_CHUTA_BY(or_52_out), .SA_2(of_hab_desab_chutes_1_sa_2),
    .SB(of_hab_desab_chutes_1_sb), .SA(of_hab_desab_chutes_1_sa), .SX(SX), .CHUTANDO_X(CHUTANDO_X), .XH(XH),
    .SB_2(of_hab_desab_chutes_1_sb_2), .YH(YH), .SY(SY), .CHUTANDO_Y(CHUTANDO_Y), .A3(in_1), .A2(in_2),
    .A1(in_3), .A0(in_4), .B3(in_5), .B2(in_6), .B1(in_7), .B0(in_8), .GA(GA), .GB(GB), .CLEAR_RESET(RESET));
  or or_59 (SA, of_hab_desab_chutes_1_sa_2, of_hab_desab_chutes_1_sa);
  or or_60 (SB, of_hab_desab_chutes_1_sb_2, of_hab_desab_chutes_1_sb);
  and and_26 (and_26_out, B_0, FF);
  and and_27 (and_27_out, ~A_0, A);  // AND_Gate
  and and_28 (and_28_out, A_0, FF);
  and and_29 (and_29_out, ~B_0, B);  // AND_Gate
  Hex_Digit_Display hex_digit_display_29 (.value(rGy));  // open: dp
  Register #(.width(4), .Select("low")) register_3 (.D(CrGy), .Q(rGy), .clk(SHOW), .clr(ALL));  // open: en
  _7_Segment_Display u_7_segment_display_11 (.g(sGy));  // open: f, a, b, e, d, c, dp
  Register #(.width(1), .Select("low")) register_4 (.D(CsGy), .Q(sGy), .clk(SHOW), .clr(ALL));  // open: en
  or or_61 (A_JOGANDO, and_26_out, and_27_out);
  or or_62 (B_JOGANDO, and_28_out, and_29_out);
  OF___Desfaz__8_a_7 of_desfaz_8_a_7_1 (.\Saída (XHDesfeito), ._3(or_63_out), ._2(XH[2]), ._1(XH[1]), ._0(XH[0]));
  or or_63 (or_63_out, XH[3], SX);
  OF___Desfaz__8_a_7 of_desfaz_8_a_7_2 (.\Saída (YHDesfeito), ._3(or_64_out), ._2(YH[2]), ._1(YH[1]), ._0(YH[0]));
  or or_64 (or_64_out, YH[3], SY);
  Hex_Digit_Display hex_digit_display_30 (.value(rGx));  // open: dp
  Register #(.width(4), .Select("low")) register_5 (.D(CrGx), .Q(rGx), .clk(SHOW), .clr(ALL));  // open: en
  _7_Segment_Display u_7_segment_display_12 (.g(sGx));  // open: f, a, b, e, d, c, dp
  Register #(.width(1), .Select("low")) register_6 (.D(CsGx), .Q(sGx), .clk(SHOW), .clr(ALL));  // open: en
  Hex_Digit_Display hex_digit_display_31 (.value(XHDesfeito));  // open: dp
  Hex_Digit_Display hex_digit_display_32 (.value(YHDesfeito));  // open: dp
  Hex_Digit_Display hex_digit_display_33 (.value(CrGx));  // open: dp
  \OF___Valor_aleatório_conv_para_valores_do_jogo  \of_valor_aleatório_conv_para_valores_do_jogo_1  (
    .\PRÓXIMO (\PRÓXIMO ), .Acertou(ACERTOU), .RESET(RESET), .Acertou_2(ACERTOU), .\PRÓXIMO_2 (\PRÓXIMO ),
    .RESET_2(RESET), .SAIDA_X(CrGx), .SX(CsGx), .SAIDAy(CrGy), .SY(CsGy));
  Hex_Digit_Display hex_digit_display_34 (.value(crx));  // open: dp
  Register #(.width(4), .Select("low")) register_7 (.D(rx), .Q(crx), .clk(SHOW), .clr(ALL));  // open: en
  _7_Segment_Display u_7_segment_display_13 (.g(register_8_q));  // open: f, a, b, e, d, c, dp
  Register #(.width(1), .Select("low")) register_8 (.Q(register_8_q), .clk(SHOW), .clr(ALL));  // open: D, en
  Hex_Digit_Display hex_digit_display_35 (.value(cry));  // open: dp
  Register #(.width(4), .Select("low")) register_9 (.D(ry), .Q(cry), .clk(SHOW), .clr(ALL));  // open: en
  _7_Segment_Display u_7_segment_display_14 (.g(register_10_q));  // open: f, a, b, e, d, c, dp
  Register #(.width(1), .Select("low")) register_10 (.Q(register_10_q), .clk(SHOW), .clr(ALL));  // open: D, en
  Hex_Digit_Display hex_digit_display_36 (.value(rCDS));  // open: dp
  Register #(.width(4), .Select("low")) register_11 (
    .D(ran_DISPLAY_CM_SOMA), .Q(rCDS), .clk(SHOW), .clr(ALL));  // open: en
  _7_Segment_Display u_7_segment_display_15 (.g(rCSS));  // open: f, a, b, e, d, c, dp
  Register #(.width(1), .Select("low")) register_12 (.D(ran_SINAL_SOMA), .Q(rCSS), .clk(SHOW), .clr(ALL));  // open: en

  // Other names for the same wires on the sheet: A0 = in_4; A1 = in_3; A2 = in_2; A3 = in_1; B0 = in_8; B1 = in_7;
  //   B2 = in_6; B3 = in_5

  // Notes on the sheet:
  //   PLACAR  DE A
  //   CRÔNOMETRO
  //   RANDOM EM HEXADECIMAL
  //   PLACAR PARA B
  //   PLACAR PARA B
  //   RANDOM -8 A 7
  //   SOMA RANDOM COORD
  //   Caso os players encontrem dificulade na hora de jogar é possível acessar os valores aleátórios clicando no botão a seguir:
  //   PLACAR DE B
  //   CRÔNOMETRO
  //   CHUTE EM HEXADECIMAL
  //   SOMA MINHAS COORD
  //   CRONÔMETRO
  //   PLACARES
  //   PECINHAS UTEIS
  //   JOGA A E B
  //   JOGA A OU  B
  //   Na parte de comparação de igualdade a soma das coordenadas  que é menor, igual ou maior....
  //   COMPARAÇÃO DA SOMA E COMPARAÇÃO DAS COORDENADAS
  //   OCULTAR/MOSTRAR SOMA E COORDENADAS ALEATÓRIAS
endmodule

// HAB5
module OF___Cronometro_p_5s (
  input  RESET,
  input  CLK,
  input  DECRESCER,
  output [3:0] \SAÍDA ,
  output CLK_SEGUINTE
);

  wire or_1_out, or_2_out;
  wire [3:0] adder_1_out, d_ff_4_q;

  Adder #(.width(4)) adder_1 (.a(d_ff_4_q), .b(4'b1111), .out(adder_1_out));  // open: cin, cout
  D_Flip_Flop d_ff_1 (.clk(or_1_out), .D(adder_1_out[3]), .Q(d_ff_4_q[3]), .reset(or_2_out));  // open: Qn, preset
  D_Flip_Flop d_ff_2 (.clk(or_1_out), .D(adder_1_out[2]), .Q(d_ff_4_q[2]), .reset(RESET));  // open: Qn, preset
  D_Flip_Flop d_ff_3 (.clk(or_1_out), .D(adder_1_out[1]), .Q(d_ff_4_q[1]), .reset(or_2_out));  // open: Qn, preset
  D_Flip_Flop d_ff_4 (.clk(or_1_out), .D(adder_1_out[0]), .Q(d_ff_4_q[0]), .reset(RESET));  // open: Qn, preset
  or or_1 (or_1_out, CLK, DECRESCER);
  or or_2 (or_2_out, RESET, CLK_SEGUINTE);
  Bit_Extender #(.in_width(4), .out_width(4), .\type ("zero")) bit_extender_1 (.in(d_ff_4_q), .out(\SAÍDA ));
  nor nor_1 (CLK_SEGUINTE, ~\SAÍDA [0], ~\SAÍDA [1], ~\SAÍDA [2], ~\SAÍDA [3]);  // NOR_Gate
  Hex_Digit_Display hex_digit_display_1 (.value(\SAÍDA ));  // open: dp
endmodule

// HAB9
module OF___Cronometro_p_9s (
  input  RESET,
  input  CLK,
  input  HAB9_0,
  output [3:0] \SAÍDA ,
  output CLK_SEGUINTE
);

  wire or_1_out, or_2_out;
  wire [3:0] adder_1_out, d_ff_4_q;

  Adder #(.width(4)) adder_1 (.a(d_ff_4_q), .b(4'b1111), .out(adder_1_out));  // open: cin, cout
  D_Flip_Flop d_ff_1 (.clk(or_1_out), .D(adder_1_out[3]), .Q(d_ff_4_q[3]), .reset(RESET));  // open: Qn, preset
  D_Flip_Flop d_ff_2 (.clk(or_1_out), .D(adder_1_out[2]), .Q(d_ff_4_q[2]), .reset(or_2_out));  // open: Qn, preset
  or or_1 (or_1_out, CLK, HAB9_0);
  D_Flip_Flop d_ff_3 (.clk(or_1_out), .D(adder_1_out[1]), .Q(d_ff_4_q[1]), .reset(or_2_out));  // open: Qn, preset
  D_Flip_Flop d_ff_4 (.clk(or_1_out), .D(adder_1_out[0]), .Q(d_ff_4_q[0]), .reset(RESET));  // open: Qn, preset
  or or_2 (or_2_out, RESET, CLK_SEGUINTE);
  Bit_Extender #(.in_width(4), .out_width(4), .\type ("zero")) bit_extender_1 (.in(d_ff_4_q), .out(\SAÍDA ));
  nor nor_1 (CLK_SEGUINTE, ~\SAÍDA [0], ~\SAÍDA [1], ~\SAÍDA [2], ~\SAÍDA [3]);  // NOR_Gate
  Hex_Digit_Display hex_digit_display_1 (.value(\SAÍDA ));  // open: dp
endmodule

// PAUSE
module OF___FlipFlopPessoal (
  input  Forca_a_1,
  input  NDA,
  input  Forca_a_0,
  output Q
);

  D_Flip_Flop d_ff_1 (.Q(Q), .preset(Forca_a_1), .reset(Forca_a_0));  // open: clk, D, Qn
endmodule

// CRONOMETRO
module OF___Cronometro (
  input  DM,
  input  UM,
  input  DS,
  input  US,
  input  START,
  input  CONFIGURAR,
  input  CLK,
  input  RESET,
  output [3:0] DM_2,
  output [3:0] UM_2,
  output [3:0] DS_2,
  output [3:0] US_2,
  output ZERO
);

  wire and_1_out, and_2_out, and_4_out, and_5_out, and_6_out, of_configura_display_de_0_a_5_2_clk_seguinte,
       of_configura_display_de_0_a_9_1_clk_seguinte, of_configura_display_de_0_a_9_2_clk_seguinte;

  OF___Configura_display_de_0_a_5 of_configura_display_de_0_a_5_1 (
    .START(START), .CONFIG_PAUSE(CONFIGURAR), .DECRES(DM), .DISPLAY(DM_2), .RESET(RESET),
    .CLK(of_configura_display_de_0_a_9_1_clk_seguinte));  // open: CLK_SEGUINTE, NDA
  OF___Configura_display_de_0_a_9 of_configura_display_de_0_a_9_1 (
    .START(START), .CONFIG_PAUSE(CONFIGURAR), .DECRES(UM),
    .CLK_SEGUINTE(of_configura_display_de_0_a_9_1_clk_seguinte), .DISPLAY(UM_2), .RESET(RESET),
    .CLK(of_configura_display_de_0_a_5_2_clk_seguinte));  // open: NDA
  OF___Configura_display_de_0_a_5 of_configura_display_de_0_a_5_2 (
    .START(START), .CONFIG_PAUSE(CONFIGURAR), .CLK_SEGUINTE(of_configura_display_de_0_a_5_2_clk_seguinte),
    .DECRES(DS), .DISPLAY(DS_2), .RESET(RESET), .CLK(of_configura_display_de_0_a_9_2_clk_seguinte));  // open: NDA
  OF___Configura_display_de_0_a_9 of_configura_display_de_0_a_9_2 (
    .START(START), .CONFIG_PAUSE(CONFIGURAR), .DECRES(US),
    .CLK_SEGUINTE(of_configura_display_de_0_a_9_2_clk_seguinte), .DISPLAY(US_2), .RESET(RESET),
    .CLK(and_1_out));  // open: NDA
  and and_1 (and_1_out, CLK, ~ZERO);  // AND_Gate
  and and_2 (and_2_out, ~US_2[0], ~US_2[1], ~US_2[2], ~US_2[3]);  // AND_Gate
  and and_3 (ZERO, and_2_out, and_4_out, and_5_out, and_6_out);
  and and_4 (and_4_out, ~DS_2[0], ~DS_2[1], ~DS_2[2], ~DS_2[3]);  // AND_Gate
  and and_5 (and_5_out, ~UM_2[0], ~UM_2[1], ~UM_2[2], ~UM_2[3]);  // AND_Gate
  and and_6 (and_6_out, ~DM_2[0], ~DM_2[1], ~DM_2[2], ~DM_2[3]);  // AND_Gate
endmodule

// all5
module OF___Configura_display_de_0_a_5 (
  input  START,
  input  CONFIG_PAUSE,
  input  RESET,
  input  NDA,
  input  DECRES,
  input  CLK,
  output [3:0] DISPLAY,
  output CLK_SEGUINTE
);

  wire and_1_out, and_2_out, flipflop_estrutural_1_q, of_flipfloppessoal_1_q;

  OF___FlipFlopPessoal of_flipfloppessoal_1 (
    .Forca_a_1(START), .Forca_a_0(CONFIG_PAUSE), .Q(of_flipfloppessoal_1_q));  // open: NDA
  flipflop_estrutural flipflop_estrutural_1 (.F1(of_flipfloppessoal_1_q), .Q(flipflop_estrutural_1_q), .F0(DECRES));
  Hex_Digit_Display hex_digit_display_1 (.value(DISPLAY));  // open: dp
  OF___Cronometro_p_5s of_cronometro_p_5s_1 (
    .CLK(and_2_out), .DECRESCER(DECRES), .RESET(RESET), .CLK_SEGUINTE(CLK_SEGUINTE), .\SAÍDA (DISPLAY));
  and and_1 (and_1_out, of_flipfloppessoal_1_q, flipflop_estrutural_1_q);
  and and_2 (and_2_out, and_1_out, CLK);
endmodule

// all9
module OF___Configura_display_de_0_a_9 (
  input  START,
  input  CONFIG_PAUSE,
  input  RESET,
  input  NDA,
  input  DECRES,
  input  CLK,
  output [3:0] DISPLAY,
  output CLK_SEGUINTE
);

  wire and_1_out, and_2_out, d_ff_1_q, of_flipfloppessoal_1_q;

  OF___FlipFlopPessoal of_flipfloppessoal_1 (
    .Forca_a_1(START), .Forca_a_0(CONFIG_PAUSE), .Q(of_flipfloppessoal_1_q));  // open: NDA
  D_Flip_Flop d_ff_1 (.Q(d_ff_1_q), .preset(of_flipfloppessoal_1_q), .reset(DECRES));  // open: clk, D, Qn
  Hex_Digit_Display hex_digit_display_1 (.value(DISPLAY));  // open: dp
  OF___Cronometro_p_9s of_cronometro_p_9s_1 (
    .CLK(and_2_out), .HAB9_0(DECRES), .\SAÍDA (DISPLAY), .RESET(RESET), .CLK_SEGUINTE(CLK_SEGUINTE));
  and and_1 (and_1_out, of_flipfloppessoal_1_q, d_ff_1_q);
  and and_2 (and_2_out, and_1_out, CLK);
endmodule

// RECEIVE
module OF___Hab_desab_chutes (
  input  A3,
  input  A2,
  input  A1,
  input  A0,
  input  B3,
  input  B2,
  input  B1,
  input  B0,
  input  HABILITA_AX,
  input  DESABILITA_CHUTA_AX,
  input  HABILITA_BX,
  input  DESABILITA_CHUTA_BX,
  input  HABILITA__AY,
  input  DESABILITA_CHUTA_AY,
  input  HABILITA__BY,
  input  DESABILITA_CHUTA_BY,
  input  CLEAR_RESET,
  output SB,
  output SA,
  output SA_2,
  output [3:0] YH,
  output SX,
  output CHUTANDO_X,
  output [3:0] XH,
  output [3:0] GA,
  output [3:0] GB,
  output SB_2,
  output SY,
  output CHUTANDO_Y
);

  wire and_4_out, ASX, ASY, BSX, BSY, KITPSAX, KITPSAY, KITPSBX, KITPSBY, or_2_out, or_3_out, or_4_out,
       or_7_out, or_9_out, or_11_out, or_14_out;
  wire [3:0] VAIPRAGAX, VAIPRAGAY, VAIPRAGBX, VAIPRAGBY, VAIPRAXHA, VAIPRAXHB, VAIPRAYHA, VAIPRAYHB, XHPORA,
       XHPORB, YHPORA, YHPORB;

  OF___Limitador_de_chute___8_a_7 of_limitador_de_chute_8_a_7_1 (
    .SINAL(SA), .\Saída (VAIPRAXHA), ._3(A3), ._2(A2), ._1(A1), ._0(A0));
  OF___Limitador_de_chute___8_a_7 of_limitador_de_chute_8_a_7_2 (
    .SINAL(SB_2), .\Saída (VAIPRAXHB), ._3(B3), ._2(B2), ._1(B1), ._0(B0));
  OF___FlipFlopPessoal of_flipfloppessoal_1 (
    .Forca_a_1(HABILITA_BX), .Forca_a_0(DESABILITA_CHUTA_BX), .Q(KITPSBX));  // open: NDA
  OF___FlipFlopPessoal of_flipfloppessoal_2 (
    .Forca_a_1(HABILITA__AY), .Forca_a_0(DESABILITA_CHUTA_AY), .Q(KITPSAY));  // open: NDA
  OF___FlipFlopPessoal of_flipfloppessoal_3 (
    .Forca_a_1(HABILITA__BY), .Forca_a_0(DESABILITA_CHUTA_BY), .Q(KITPSBY));  // open: NDA
  OF___FlipFlopPessoal of_flipfloppessoal_4 (
    .Forca_a_1(HABILITA_AX), .Forca_a_0(DESABILITA_CHUTA_AX), .Q(KITPSAX));  // open: NDA
  Register #(.width(4), .Select("low")) register_1 (
    .D(VAIPRAXHA), .Q(XHPORA), .clk(DESABILITA_CHUTA_AX), .clr(or_2_out));  // open: en
  assign XH = XHPORA | XHPORB;  // OR_Gate or_1, 4 bits wide
  Register #(.width(1), .Select("low")) ARMAZENA_SINAL (
    .D(SA), .Q(ASX), .clk(DESABILITA_CHUTA_AX), .clr(or_2_out));  // open: en
  or or_2 (or_2_out, HABILITA_BX, CLEAR_RESET);
  Register #(.width(4), .Select("low")) register_2 (
    .D(VAIPRAXHB), .Q(XHPORB), .clk(DESABILITA_CHUTA_BX), .clr(or_3_out));  // open: en
  or or_3 (or_3_out, CLEAR_RESET, HABILITA_AX);
  Register #(.width(1), .Select("low")) register_3 (
    .D(SB_2), .Q(BSX), .clk(DESABILITA_CHUTA_BX), .clr(or_4_out));  // open: en
  or or_4 (or_4_out, HABILITA_AX, CLEAR_RESET);
  or or_5 (SX, ASX, BSX);
  assign VAIPRAGAX = VAIPRAXHA & {4{KITPSAX}};  // AND_Gate and_1, 4 bits wide
  assign VAIPRAGAY = VAIPRAYHA & {4{KITPSAY}};  // AND_Gate and_2, 4 bits wide
  and and_3 (SA_2, A3, KITPSAY);
  assign GA = VAIPRAGAX | VAIPRAGAY;  // OR_Gate or_6, 4 bits wide
  Register #(.width(4), .Select("low")) register_4 (
    .D(VAIPRAYHA), .Q(YHPORA), .clk(DESABILITA_CHUTA_AY), .clr(or_7_out));  // open: en
  or or_7 (or_7_out, HABILITA__BY, CLEAR_RESET);
  OF___Limitador_de_chute___8_a_7 of_limitador_de_chute_8_a_7_3 (
    .\Saída (VAIPRAYHA), ._3(A3), ._2(A2), ._1(A1), ._0(A0));  // open: SINAL
  buf and_4 (and_4_out, KITPSAX);  // AND_Gate AND_Gate
  assign GB = VAIPRAGBX | VAIPRAGBY;  // OR_Gate or_8, 4 bits wide
  assign VAIPRAGBX = VAIPRAXHB & {4{KITPSBX}};  // AND_Gate and_5, 4 bits wide
  Register #(.width(1), .Select("low")) register_5 (
    .D(SA_2), .Q(ASY), .clk(DESABILITA_CHUTA_AY), .clr(or_9_out));  // open: en
  or or_9 (or_9_out, HABILITA__BY, CLEAR_RESET);
  or or_10 (CHUTANDO_X, and_4_out, KITPSBX);
  assign VAIPRAGBY = VAIPRAYHB & {4{KITPSBY}};  // AND_Gate and_6, 4 bits wide
  Register #(.width(4), .Select("low")) armazena_valor_de_b_y (
    .D(VAIPRAYHB), .Q(YHPORB), .clk(DESABILITA_CHUTA_BY), .clr(or_11_out));  // open: en
  or or_11 (or_11_out, HABILITA__AY, CLEAR_RESET);
  assign YH = YHPORA | YHPORB;  // OR_Gate or_12, 4 bits wide
  or or_13 (CHUTANDO_Y, KITPSAY, KITPSBY);
  OF___Limitador_de_chute___8_a_7 of_limitador_de_chute_8_a_7_4 (
    .SINAL(SB), .\Saída (VAIPRAYHB), ._3(B3), ._2(B2), ._1(B1), ._0(B0));
  or or_14 (or_14_out, HABILITA__AY, CLEAR_RESET);
  or or_15 (SY, ASY, BSY);
  Register #(.width(1), .Select("low")) armazena_sinal_b_y (
    .D(SB), .Q(BSY), .clk(DESABILITA_CHUTA_BY), .clr(or_14_out));  // open: en

  // Other names for the same wires on the sheet: CLEART = CLEAR_RESET; DESABAX = DESABILITA_CHUTA_AX;
  //   DESABAY = DESABILITA_CHUTA_AY; DESABBX = DESABILITA_CHUTA_BX; DESABBY = DESABILITA_CHUTA_BY;
  //   HABAX = HABILITA_AX; HABAY = HABILITA__AY; HABBX = HABILITA_BX; HABBY = HABILITA__BY; SA1 = SA; SAA = SA_2;
  //   SB1 = SB_2; SBY = SB
endmodule

module OF___Limitador_de_valores_p_chute (
  input  _3,
  input  _2,
  input  _1,
  input  _0,
  output [3:0] \Saída ,
  output SINAL
);

  wire and_1_out, and_2_out, and_3_out, and_4_out, and_5_out, and_6_out, not_1_out, not_2_out, not_3_out,
       not_4_out, or_1_out, or_2_out;
  wire [3:0] adder_1_out, d_ff_4_q;

  Adder #(.width(4)) adder_1 (.a(d_ff_4_q), .b(4'b0001), .out(adder_1_out));  // open: cin, cout
  D_Flip_Flop d_ff_1 (.D(adder_1_out[3]), .Q(d_ff_4_q[3]), .preset(_3), .reset(or_1_out));  // open: clk, Qn
  not not_1 (not_1_out, _3);
  or or_1 (or_1_out, not_1_out, and_2_out, or_2_out, and_4_out, and_1_out, and_3_out);
  or or_2 (or_2_out, and_5_out, and_6_out);
  D_Flip_Flop d_ff_2 (.D(adder_1_out[2]), .Q(d_ff_4_q[2]), .preset(_2), .reset(not_2_out));  // open: clk, Qn
  not not_2 (not_2_out, _2);
  D_Flip_Flop d_ff_3 (.D(adder_1_out[1]), .Q(d_ff_4_q[1]), .preset(_1), .reset(not_3_out));  // open: clk, Qn
  not not_3 (not_3_out, _1);
  Bit_Extender #(.in_width(4), .out_width(4), .\type ("zero")) bit_extender_1 (.in(d_ff_4_q), .out(\Saída ));
  and and_1 (and_1_out, _3, _2, _1);
  and and_2 (and_2_out, _3, _1, _0, _2);
  D_Flip_Flop d_ff_4 (.D(adder_1_out[0]), .Q(d_ff_4_q[0]), .preset(_0), .reset(not_4_out));  // open: clk, Qn
  not not_4 (not_4_out, _0);
  Hex_Digit_Display hex_digit_display_1 (.value(\Saída ));  // open: dp
  and and_3 (and_3_out, _1, _3, _0);
  and and_4 (and_4_out, _3, _1);
  and and_5 (and_5_out, _3, _0);
  and and_6 (and_6_out, _3, _2);

  assign SINAL = _3;
endmodule

// Comparador Soma
module OF___Comparador_soma (
  input  [3:0] DISPLAY_COM_SOMA,
  input  sinal_soma,
  input  [3:0] RAND_SOMA,
  input  rSS,
  input  CHUTE,
  input  START,
  output out_7,
  output [3:0] out_8,
  output IGUAL,
  output out_10,
  output [3:0] out_11,
  output A___B___RANDOM___MEU,
  output A___B___RANDOM___MEU_2
);

  wire and_1_out, and_2_out, and_3_out, and_4_out, and_5_out, and_6_out, and_7_out, and_8_out, and_9_out,
       and_10_out, and_11_out, and_12_out, of_comparador_1_a__random___maior_que_b__meu,
       of_comparador_1_a__random___menor_que_b__meu, of_comparador_1_igual, or_1_out, or_2_out, or_3_out;

  _7_Segment_Display u_7_segment_display_1 (.g(sinal_soma));  // open: f, a, b, e, d, c, dp
  Hex_Digit_Display hex_digit_display_1 (.value(DISPLAY_COM_SOMA));  // open: dp
  _7_Segment_Display u_7_segment_display_2 (.g(rSS));  // open: f, a, b, e, d, c, dp
  OF___Comparador of_comparador_1 (
    .Igual(of_comparador_1_igual),
    .A__random___MENOR_que_B__meu(of_comparador_1_a__random___menor_que_b__meu), .P(DISPLAY_COM_SOMA),
    .R(RAND_SOMA), .A__random___MAIOR_que_B__meu(of_comparador_1_a__random___maior_que_b__meu));
  Hex_Digit_Display hex_digit_display_2 (.value(RAND_SOMA));  // open: dp
  and and_1 (and_1_out, ~sinal_soma, ~rSS, of_comparador_1_igual);  // AND_Gate
  and and_2 (and_2_out, sinal_soma, ~rSS, of_comparador_1_igual);  // AND_Gate
  and and_3 (and_3_out, ~sinal_soma, rSS, of_comparador_1_igual);  // AND_Gate
  and and_4 (and_4_out, sinal_soma, rSS, of_comparador_1_igual);
  and and_5 (and_5_out, ~sinal_soma, rSS, of_comparador_1_a__random___maior_que_b__meu);  // AND_Gate
  and and_6 (and_6_out, ~sinal_soma, ~rSS, of_comparador_1_a__random___maior_que_b__meu);  // AND_Gate
  and and_7 (and_7_out, sinal_soma, rSS, of_comparador_1_a__random___maior_que_b__meu);
  and and_8 (and_8_out, sinal_soma, ~rSS, of_comparador_1_a__random___maior_que_b__meu);  // AND_Gate
  and and_9 (and_9_out, ~sinal_soma, rSS, of_comparador_1_a__random___menor_que_b__meu);  // AND_Gate
  and and_10 (and_10_out, ~sinal_soma, ~rSS, of_comparador_1_a__random___menor_que_b__meu);  // AND_Gate
  and and_11 (and_11_out, sinal_soma, rSS, of_comparador_1_a__random___menor_que_b__meu);
  and and_12 (and_12_out, sinal_soma, ~rSS, of_comparador_1_a__random___menor_que_b__meu);  // AND_Gate
  or or_1 (or_1_out, and_1_out, and_4_out);
  or or_2 (or_2_out, and_2_out, and_6_out, and_8_out, and_11_out, and_12_out);
  and and_13 (A___B___RANDOM___MEU_2, or_2_out, CHUTE, START);
  and and_14 (IGUAL, or_1_out, CHUTE, START);
  or or_3 (or_3_out, and_3_out, and_5_out, and_7_out, and_9_out, and_10_out);
  and and_15 (A___B___RANDOM___MEU, or_3_out, CHUTE, START);

  assign out_7 = sinal_soma;
  assign out_8 = DISPLAY_COM_SOMA;
  assign out_10 = rSS;
  assign out_11 = RAND_SOMA;

  // Other names for the same wires on the sheet: DISPLAY_CM_SOMA[3:0] = DISPLAY_COM_SOMA;
  //   DISPLAY_CM_SOMARAND[3:0] = RAND_SOMA; SINAL_SOMARAND = rSS

  // Notes on the sheet:
  //   MEU
  //   RANDOM
endmodule

// Acertou?
module OF___Verificar_se_acertou (
  input  \PRÓXIMO ,
  input  Acertou,
  input  RESET,
  input  [3:0] chute_x,
  input  [3:0] chute_y,
  input  CHUTE,
  input  Acertou_2,
  input  \PRÓXIMO_2 ,
  input  RESET_2,
  output [3:0] SAIDA_X,
  output Acertou_3,
  output [3:0] SAIDA
);

  wire and_1_out, d_ff_1_q, flipflop_estrutural_1_q, of_comparador_1_igual, of_comparador_2_igual, or_1_out,
       or_2_out;

  flipflop_estrutural flipflop_estrutural_1 (.F1(Acertou), .Q(flipflop_estrutural_1_q), .F0(or_1_out));
  or or_1 (or_1_out, RESET, \PRÓXIMO );
  or or_2 (or_2_out, RESET_2, \PRÓXIMO_2 );
  D_Flip_Flop d_ff_1 (.Q(d_ff_1_q), .preset(Acertou_2), .reset(or_2_out));  // open: clk, D, Qn
  Random #(.width(4), .seed(1)) Random_X (.clk(\PRÓXIMO_2 ), .next(d_ff_1_q), .out(SAIDA), .clr(RESET_2));
  Random #(.width(4)) Random_X_2 (.clk(\PRÓXIMO ), .next(flipflop_estrutural_1_q), .out(SAIDA_X), .clr(RESET));
  OF___Comparador of_comparador_1 (
    .Igual(of_comparador_1_igual), .P(chute_x), .R(SAIDA_X));  // open: A__random___MENOR_que_B__meu, A__random___MAIOR_que_B__meu
  OF___Comparador of_comparador_2 (
    .Igual(of_comparador_2_igual), .P(chute_y), .R(SAIDA));  // open: A__random___MENOR_que_B__meu, A__random___MAIOR_que_B__meu
  and and_1 (and_1_out, of_comparador_1_igual, of_comparador_2_igual);
  and and_2 (Acertou_3, and_1_out, CHUTE);
endmodule

// 5
module OF___Placar_para_dezenas (
  input  Botton,
  input  RESET,
  output [3:0] \SAÍDA_P__DISPLAY 
);

  wire [3:0] adder_1_out, d_ff_4_q;

  Adder #(.width(4)) adder_1 (.a(d_ff_4_q), .b(4'b0001), .out(adder_1_out));  // open: cin, cout
  D_Flip_Flop d_ff_1 (.clk(Botton), .D(adder_1_out[3]), .Q(d_ff_4_q[3]), .reset(RESET));  // open: Qn, preset
  D_Flip_Flop d_ff_2 (.clk(Botton), .D(adder_1_out[2]), .Q(d_ff_4_q[2]), .reset(RESET));  // open: Qn, preset
  D_Flip_Flop d_ff_3 (.clk(Botton), .D(adder_1_out[1]), .Q(d_ff_4_q[1]), .reset(RESET));  // open: Qn, preset
  D_Flip_Flop d_ff_4 (.clk(Botton), .D(adder_1_out[0]), .Q(d_ff_4_q[0]), .reset(RESET));  // open: Qn, preset
  Bit_Extender #(.in_width(4), .out_width(4), .\type ("zero")) bit_extender_1 (.in(d_ff_4_q), .out(\SAÍDA_P__DISPLAY ));
  Hex_Digit_Display hex_digit_display_1 (.value(\SAÍDA_P__DISPLAY ));  // open: dp
endmodule

// 9
module OF___Placar_para_unidades (
  input  Botton,
  input  RESET,
  output [3:0] \SAÍDA_P__DISPLAY ,
  output PLACAR2
);

  wire or_1_out;
  wire [3:0] adder_1_out, d_ff_4_q;

  Adder #(.width(4)) adder_1 (.a(d_ff_4_q), .b(4'b0001), .out(adder_1_out));  // open: cin, cout
  D_Flip_Flop d_ff_1 (.clk(Botton), .D(adder_1_out[3]), .Q(d_ff_4_q[3]), .reset(or_1_out));  // open: Qn, preset
  D_Flip_Flop d_ff_2 (.clk(Botton), .D(adder_1_out[2]), .Q(d_ff_4_q[2]), .reset(or_1_out));  // open: Qn, preset
  D_Flip_Flop d_ff_3 (.clk(Botton), .D(adder_1_out[1]), .Q(d_ff_4_q[1]), .reset(or_1_out));  // open: Qn, preset
  D_Flip_Flop d_ff_4 (.clk(Botton), .D(adder_1_out[0]), .Q(d_ff_4_q[0]), .reset(or_1_out));  // open: Qn, preset
  or or_1 (or_1_out, PLACAR2, RESET);
  Bit_Extender #(.in_width(4), .out_width(4), .\type ("zero")) bit_extender_1 (.in(d_ff_4_q), .out(\SAÍDA_P__DISPLAY ));
  and and_1 (PLACAR2, ~\SAÍDA_P__DISPLAY [0], \SAÍDA_P__DISPLAY [1], ~\SAÍDA_P__DISPLAY [2], \SAÍDA_P__DISPLAY [3]);  // AND_Gate
  Hex_Digit_Display hex_digit_display_1 (.value(\SAÍDA_P__DISPLAY ));  // open: dp
endmodule

module OF___FlipFlop_D_pessoal (
  input  F1,
  input  nda,
  input  F0,
  output Q
);

  wire and_1_out, and_2_out, and_3_out, and_4_out, not_1_out, not_2_out, not_4_out;

  not not_1 (not_1_out, and_1_out);
  buf and_1 (and_1_out, F1);  // AND_Gate
  not not_2 (not_2_out, and_2_out);
  buf and_2 (and_2_out, F0);  // AND_Gate
  not not_3 (Q, and_3_out);
  and and_3 (and_3_out, not_1_out, not_4_out);
  and and_4 (and_4_out, Q, not_2_out);
  not not_4 (not_4_out, and_4_out);
endmodule

// GBPC
module \OF___Gerar_bit_para_próximo_chute  (
  input  START,
  input  RESET,
  input  \PRÓXIMO ,
  output [3:0] \SAÍDA 
);

  wire or_1_out, or_2_out, or_3_out;
  wire [3:0] adder_1_out, d_ff_4_q;

  or or_1 (or_1_out, RESET, START);
  Adder #(.width(4)) adder_1 (.a(d_ff_4_q), .b(4'b0001), .out(adder_1_out));  // open: cin, cout
  D_Flip_Flop d_ff_1 (.clk(\PRÓXIMO ), .D(adder_1_out[3]), .Q(d_ff_4_q[3]), .reset(or_3_out));  // open: Qn, preset
  D_Flip_Flop d_ff_2 (.clk(\PRÓXIMO ), .D(adder_1_out[2]), .Q(d_ff_4_q[2]), .reset(or_1_out));  // open: Qn, preset
  D_Flip_Flop d_ff_3 (.clk(\PRÓXIMO ), .D(adder_1_out[1]), .Q(d_ff_4_q[1]), .reset(or_2_out));  // open: Qn, preset
  D_Flip_Flop d_ff_4 (.clk(\PRÓXIMO ), .D(adder_1_out[0]), .Q(d_ff_4_q[0]), .preset(START), .reset(RESET));  // open: Qn
  or or_2 (or_2_out, START, RESET);
  or or_3 (or_3_out, START, RESET);
  Bit_Extender #(.in_width(4), .out_width(4), .\type ("zero")) bit_extender_1 (.in(d_ff_4_q), .out(\SAÍDA ));
  Hex_Digit_Display hex_digit_display_1 (.value(\SAÍDA ));  // open: dp
endmodule

// NEXT/KICK
module \OF___Botão_para_próximo_ou_chute  (
  input  START,
  input  CHUTE,
  input  \PRÓXIMO ,
  input  RESET,
  output HABILITA_AX,
  output HABILITA_AY,
  output COMPARA,
  output HABILITA_BX,
  output HABILITA_BY,
  output COMPARA_2,
  output CHUTA_AY,
  output CHUTA_BX,
  output CHUTA_BY,
  output CHUTA_AX
);

  wire and_1_out, and_3_out, and_6_out, and_10_out, and_13_out, d_ff_1_q, d_ff_2_q, or_1_out, or_2_out;
  wire [3:0] \of_gerar_bit_para_próximo_chute_1_saída ;

  or or_1 (or_1_out, CHUTE, \PRÓXIMO );
  D_Flip_Flop d_ff_1 (.Q(d_ff_1_q), .preset(CHUTE), .reset(\PRÓXIMO ));  // open: clk, D, Qn
  \OF___Gerar_bit_para_próximo_chute  \of_gerar_bit_para_próximo_chute_1  (
    .\PRÓXIMO (or_1_out), .START(or_2_out), .RESET(RESET), .\SAÍDA (\of_gerar_bit_para_próximo_chute_1_saída ));
  D_Flip_Flop d_ff_2 (.Q(d_ff_2_q), .preset(\PRÓXIMO ), .reset(CHUTE));  // open: clk, D, Qn
  Hex_Digit_Display hex_digit_display_1 (.value(\of_gerar_bit_para_próximo_chute_1_saída ));  // open: dp
  and and_1 (and_1_out, \of_gerar_bit_para_próximo_chute_1_saída [3], ~\of_gerar_bit_para_próximo_chute_1_saída [2], \of_gerar_bit_para_próximo_chute_1_saída [1], \of_gerar_bit_para_próximo_chute_1_saída [0]);  // AND_Gate
  or or_2 (or_2_out, START, and_1_out);
  and and_2 (HABILITA_AX, ~\of_gerar_bit_para_próximo_chute_1_saída [3], ~\of_gerar_bit_para_próximo_chute_1_saída [2], ~\of_gerar_bit_para_próximo_chute_1_saída [1], \of_gerar_bit_para_próximo_chute_1_saída [0]);  // AND_Gate
  and and_3 (and_3_out, ~\of_gerar_bit_para_próximo_chute_1_saída [3], ~\of_gerar_bit_para_próximo_chute_1_saída [2], \of_gerar_bit_para_próximo_chute_1_saída [1], ~\of_gerar_bit_para_próximo_chute_1_saída [0]);  // AND_Gate
  and and_4 (CHUTA_AX, and_3_out, d_ff_1_q);
  and and_5 (HABILITA_AY, ~\of_gerar_bit_para_próximo_chute_1_saída [3], ~\of_gerar_bit_para_próximo_chute_1_saída [2], \of_gerar_bit_para_próximo_chute_1_saída [1], \of_gerar_bit_para_próximo_chute_1_saída [0]);  // AND_Gate
  and and_6 (and_6_out, ~\of_gerar_bit_para_próximo_chute_1_saída [3], \of_gerar_bit_para_próximo_chute_1_saída [2], ~\of_gerar_bit_para_próximo_chute_1_saída [1], ~\of_gerar_bit_para_próximo_chute_1_saída [0]);  // AND_Gate
  and and_7 (CHUTA_AY, and_6_out, d_ff_1_q);
  and and_8 (COMPARA, ~\of_gerar_bit_para_próximo_chute_1_saída [3], \of_gerar_bit_para_próximo_chute_1_saída [2], ~\of_gerar_bit_para_próximo_chute_1_saída [1], \of_gerar_bit_para_próximo_chute_1_saída [0]);  // AND_Gate
  and and_9 (HABILITA_BX, ~\of_gerar_bit_para_próximo_chute_1_saída [3], \of_gerar_bit_para_próximo_chute_1_saída [2], \of_gerar_bit_para_próximo_chute_1_saída [1], ~\of_gerar_bit_para_próximo_chute_1_saída [0]);  // AND_Gate
  and and_10 (and_10_out, ~\of_gerar_bit_para_próximo_chute_1_saída [3], \of_gerar_bit_para_próximo_chute_1_saída [2], \of_gerar_bit_para_próximo_chute_1_saída [1], \of_gerar_bit_para_próximo_chute_1_saída [0]);  // AND_Gate
  and and_11 (CHUTA_BX, and_10_out, d_ff_1_q);
  and and_12 (HABILITA_BY, \of_gerar_bit_para_próximo_chute_1_saída [3], ~\of_gerar_bit_para_próximo_chute_1_saída [2], ~\of_gerar_bit_para_próximo_chute_1_saída [1], ~\of_gerar_bit_para_próximo_chute_1_saída [0]);  // AND_Gate
  and and_13 (and_13_out, \of_gerar_bit_para_próximo_chute_1_saída [3], ~\of_gerar_bit_para_próximo_chute_1_saída [2], ~\of_gerar_bit_para_próximo_chute_1_saída [1], \of_gerar_bit_para_próximo_chute_1_saída [0]);  // AND_Gate
  and and_14 (CHUTA_BY, and_13_out, d_ff_1_q);
  and and_15 (COMPARA_2, \of_gerar_bit_para_próximo_chute_1_saída [3], ~\of_gerar_bit_para_próximo_chute_1_saída [2], \of_gerar_bit_para_próximo_chute_1_saída [1], ~\of_gerar_bit_para_próximo_chute_1_saída [0]);  // AND_Gate
endmodule

// LIMITEKICK
module OF___Limitador_de_valores_p_pontuacao (
  input  _3,
  input  _2,
  input  _1,
  input  _0,
  output [3:0] \Saída ,
  output out_6
);

  wire and_1_out, and_2_out, and_3_out, and_4_out, and_5_out, and_6_out, not_1_out, not_2_out, not_3_out,
       not_4_out, or_1_out, or_2_out, or_3_out, or_4_out, or_5_out;
  wire [3:0] adder_1_out, d_ff_4_q;

  Adder #(.width(4)) adder_1 (.a(d_ff_4_q), .b(4'b0001), .out(adder_1_out));  // open: cin, cout
  D_Flip_Flop d_ff_1 (.D(adder_1_out[3]), .Q(d_ff_4_q[3]), .preset(_3), .reset(or_1_out));  // open: clk, Qn
  not not_1 (not_1_out, _3);
  or or_1 (or_1_out, not_1_out, and_2_out, or_2_out, and_4_out, and_1_out, and_3_out);
  or or_2 (or_2_out, and_5_out, and_6_out);
  D_Flip_Flop d_ff_2 (.D(adder_1_out[2]), .Q(d_ff_4_q[2]), .preset(_2), .reset(or_3_out));  // open: clk, Qn
  buf or_3 (or_3_out, not_2_out);  // OR_Gate
  not not_2 (not_2_out, _2);
  D_Flip_Flop d_ff_3 (.D(adder_1_out[1]), .Q(d_ff_4_q[1]), .preset(_1), .reset(or_4_out));  // open: clk, Qn
  not not_3 (not_3_out, _1);
  buf or_4 (or_4_out, not_3_out);  // OR_Gate
  Bit_Extender #(.in_width(4), .out_width(4), .\type ("zero")) bit_extender_1 (.in(d_ff_4_q), .out(\Saída ));
  and and_1 (and_1_out, _3, _2, _1);
  and and_2 (and_2_out, _3, _1, _0, _2);
  D_Flip_Flop d_ff_4 (.D(adder_1_out[0]), .Q(d_ff_4_q[0]), .preset(_0), .reset(or_5_out));  // open: clk, Qn
  buf or_5 (or_5_out, not_4_out);  // OR_Gate
  Hex_Digit_Display hex_digit_display_1 (.value(\Saída ));  // open: dp
  and and_3 (and_3_out, _1, _3, _0);
  not not_4 (not_4_out, _0);
  and and_4 (and_4_out, _3, _1);
  and and_5 (and_5_out, _3, _0);
  and and_6 (and_6_out, _3, _2);

  assign out_6 = _3;
endmodule

// INDIVIDUAL
module \OF___Botão_para_casos_individuais  (
  input  START,
  input  CHUTE,
  input  \PRÓXIMO ,
  input  RESET,
  output HABILITA_AX,
  output HABILITA_Y,
  output COMPARA,
  output CHUTA_Y,
  output CHUTA_X
);

  wire and_1_out, and_3_out, and_6_out, d_ff_1_q, or_1_out, or_2_out;
  wire [3:0] \of_gerar_bit_para_próximo_chute_1_saída ;

  or or_1 (or_1_out, CHUTE, \PRÓXIMO );
  D_Flip_Flop d_ff_1 (.Q(d_ff_1_q), .preset(CHUTE), .reset(\PRÓXIMO ));  // open: clk, D, Qn
  \OF___Gerar_bit_para_próximo_chute  \of_gerar_bit_para_próximo_chute_1  (
    .\PRÓXIMO (or_1_out), .START(or_2_out), .RESET(RESET), .\SAÍDA (\of_gerar_bit_para_próximo_chute_1_saída ));
  D_Flip_Flop d_ff_2 (.preset(\PRÓXIMO ), .reset(CHUTE));  // open: clk, D, Q, Qn
  Hex_Digit_Display hex_digit_display_1 (.value(\of_gerar_bit_para_próximo_chute_1_saída ));  // open: dp
  and and_1 (and_1_out, ~\of_gerar_bit_para_próximo_chute_1_saída [3], \of_gerar_bit_para_próximo_chute_1_saída [2], \of_gerar_bit_para_próximo_chute_1_saída [1], ~\of_gerar_bit_para_próximo_chute_1_saída [0]);  // AND_Gate
  or or_2 (or_2_out, START, and_1_out);
  and and_2 (HABILITA_AX, ~\of_gerar_bit_para_próximo_chute_1_saída [3], ~\of_gerar_bit_para_próximo_chute_1_saída [2], ~\of_gerar_bit_para_próximo_chute_1_saída [1], \of_gerar_bit_para_próximo_chute_1_saída [0]);  // AND_Gate
  and and_3 (and_3_out, ~\of_gerar_bit_para_próximo_chute_1_saída [3], ~\of_gerar_bit_para_próximo_chute_1_saída [2], \of_gerar_bit_para_próximo_chute_1_saída [1], ~\of_gerar_bit_para_próximo_chute_1_saída [0]);  // AND_Gate
  and and_4 (CHUTA_X, and_3_out, d_ff_1_q);
  and and_5 (HABILITA_Y, ~\of_gerar_bit_para_próximo_chute_1_saída [3], ~\of_gerar_bit_para_próximo_chute_1_saída [2], \of_gerar_bit_para_próximo_chute_1_saída [1], \of_gerar_bit_para_próximo_chute_1_saída [0]);  // AND_Gate
  and and_6 (and_6_out, ~\of_gerar_bit_para_próximo_chute_1_saída [3], \of_gerar_bit_para_próximo_chute_1_saída [2], ~\of_gerar_bit_para_próximo_chute_1_saída [1], ~\of_gerar_bit_para_próximo_chute_1_saída [0]);  // AND_Gate
  and and_7 (CHUTA_Y, and_6_out, d_ff_1_q);
  and and_8 (COMPARA, ~\of_gerar_bit_para_próximo_chute_1_saída [3], \of_gerar_bit_para_próximo_chute_1_saída [2], ~\of_gerar_bit_para_próximo_chute_1_saída [1], \of_gerar_bit_para_próximo_chute_1_saída [0]);  // AND_Gate
endmodule

// Limitador chute
module OF___Limitador_de_chute___8_a_7 (
  input  _3,
  input  _2,
  input  _1,
  input  _0,
  output SINAL,
  output [3:0] \Saída 
);

  wire _03, _013, _13, _23, _0123, _123, cin0, cin1, cin2, cin3, cout0, cout1, cout2, cout3, not_1_out,
       not_2_out, not_3_out, not_4_out, or_1_out;

  Adder #(.width(4)) adder_1 (
    .a({cin3, cin2, cin1, cin0}), .b(4'b0001), .out({cout3, cout2, cout1, cout0}));  // open: cin, cout
  D_Flip_Flop d_ff_1 (.D(cout3), .Q(cin3), .preset(_3), .reset(or_1_out));  // open: clk, Qn
  or or_1 (or_1_out, not_2_out, _03, _13, _23, _013, _123, _0123);
  D_Flip_Flop d_ff_2 (.D(cout2), .Q(cin2), .preset(_2), .reset(not_1_out));  // open: clk, Qn
  not not_1 (not_1_out, _2);
  not not_2 (not_2_out, _3);
  D_Flip_Flop d_ff_3 (.D(cout1), .Q(cin1), .preset(_1), .reset(not_3_out));  // open: clk, Qn
  not not_3 (not_3_out, _1);
  D_Flip_Flop d_ff_4 (.D(cout0), .Q(cin0), .preset(_0), .reset(not_4_out));  // open: clk, Qn
  not not_4 (not_4_out, _0);
  Bit_Extender #(.in_width(4), .out_width(4), .\type ("zero")) bit_extender_1 (
    .in({cin3, cin2, cin1, cin0}), .out(\Saída ));
  Hex_Digit_Display hex_digit_display_1 (.value(\Saída ));  // open: dp
  and and_1 (_0123, _0, _2, _1, _3);
  and and_2 (_013, _0, _1, _3);
  and and_3 (_13, _3, _1);
  and and_4 (_03, _0, _3);
  and and_5 (_23, _2, _3);
  and and_6 (_123, _1, _2, _3);

  assign SINAL = _3;
endmodule

// Desfaz limite chute
module OF___Desfaz__8_a_7 (
  input  _3,
  input  _2,
  input  _1,
  input  _0,
  output [3:0] \Saída 
);

  wire _03, _013, _13, _23, _0123, _123, cin0, cin1, cin2, cin3, cout0, cout1, cout2, cout3, not_1_out,
       not_2_out, not_3_out, not_4_out, or_1_out;

  Adder #(.width(4)) adder_1 (
    .a({cin3, cin2, cin1, cin0}), .b(4'b0001), .out({cout3, cout2, cout1, cout0}));  // open: cin, cout
  D_Flip_Flop d_ff_1 (.D(cout3), .Q(cin3), .preset(or_1_out), .reset(not_2_out));  // open: clk, Qn
  D_Flip_Flop d_ff_2 (.D(cout2), .Q(cin2), .preset(_2), .reset(not_1_out));  // open: clk, Qn
  not not_1 (not_1_out, _2);
  not not_2 (not_2_out, _3);
  or or_1 (or_1_out, _3, _03, _13, _23, _013, _123, _0123);
  D_Flip_Flop d_ff_3 (.D(cout1), .Q(cin1), .preset(_1), .reset(not_3_out));  // open: clk, Qn
  not not_3 (not_3_out, _1);
  D_Flip_Flop d_ff_4 (.D(cout0), .Q(cin0), .preset(_0), .reset(not_4_out));  // open: clk, Qn
  not not_4 (not_4_out, _0);
  Bit_Extender #(.in_width(4), .out_width(4), .\type ("zero")) bit_extender_1 (
    .in({cin3, cin2, cin1, cin0}), .out(\Saída ));
  Hex_Digit_Display hex_digit_display_1 (.value(\Saída ));  // open: dp
  and and_1 (_0123, _0, _2, _1, _3);
  and and_2 (_013, _0, _1, _3);
  and and_3 (_13, _3, _1);
  and and_4 (_03, _0, _3);
  and and_5 (_23, _2, _3);
  and and_6 (_123, _1, _2, _3);
endmodule

// Possib table
module OF___Tabela_de_possibilidades_de_soma (
  input  [3:0] A,
  input  [3:0] B,
  output SINAL_SOMA,
  output [3:0] DISPLAY_SOMA
);

  wire A_MAIOR_Q_B, A_MENOR_Q_B, A_PODE_SER_IGUAL_A_B, and_6_out, and_20_out, DIFERENTES, KICK, NEG,
       not_1_out, not_2_out, not_3_out, not_4_out, not_5_out, not_6_out, not_7_out, not_8_out, not_9_out,
       not_10_out, not_11_out, not_12_out, not_13_out, not_14_out, not_15_out, not_16_out, POS,
       S_A_B_NEGATIVOS_E_DIFERENTES, SA, SA_B_NEG__IGUAIS, SB;
  wire [3:0] A_B, A_B_NEG__IGUAIS, A_B_NEGATIVOS_E_DIFERENTES, A_B_POS_EM_A_IGUAIS, A_B_POS_EM_B_IGUAIS,
       A_B_POS_IGUAIS, A_B_POSITIVOS_E_DIFERENTES, A_B_t, and_7_out, and_11_out, and_13_out, and_17_out, B_A,
       SAIDA_A, SAIDA_B, SPOS;

  Button button_1 (.out(KICK));
  _7_Segment_Display u_7_segment_display_1 (.g(SINAL_SOMA));  // open: f, a, b, e, d, c, dp
  Adder #(.width(4)) adder_1 (.a(SAIDA_A), .b(SAIDA_B), .out(SPOS));  // open: cin, cout
  and and_1 (POS, ~B[3], ~A[3]);  // AND_Gate
  and and_2 (NEG, B[3], A[3]);
  Hex_Digit_Display hex_digit_display_1 (.value(DISPLAY_SOMA));  // open: dp
  Comparator #(.width(4)) comparator_1 (
    .a(SAIDA_A), .b(SAIDA_B), .gt(A_MAIOR_Q_B), .eq(A_PODE_SER_IGUAL_A_B), .lt(A_MENOR_Q_B));
  Adder #(.width(4)) adder_2 (.a(SAIDA_A), .b(SAIDA_B), .out(A_B));  // open: cin, cout
  _7_Segment_Display u_7_segment_display_2 (.g(A[3]));  // open: f, a, b, e, d, c, dp
  OF___Limitador_de_chute___8_a_7 of_limitador_de_chute_8_a_7_1 (
    .SINAL(SA), .\Saída (SAIDA_A), ._3(A[3]), ._2(A[2]), ._1(A[1]), ._0(A[0]));
  OF___Limitador_de_chute___8_a_7 of_limitador_de_chute_8_a_7_2 (
    .SINAL(SB), .\Saída (SAIDA_B), ._3(B[3]), ._2(B[2]), ._1(B[1]), ._0(B[0]));
  _7_Segment_Display u_7_segment_display_3 (.g(SB));  // open: f, a, b, e, d, c, dp
  Hex_Digit_Display hex_digit_display_2 (.value(SAIDA_A));  // open: dp
  Subtractor #(.width(4)) subtractor_1 (.a(SAIDA_A), .b(SAIDA_B), .out(A_B_t));  // open: bin, bout
  Subtractor #(.width(4)) subtractor_2 (.a(SAIDA_B), .b(SAIDA_A), .out(B_A));  // open: bin, bout
  Hex_Digit_Display hex_digit_display_3 (.value(SAIDA_B));  // open: dp
  or or_1 (DIFERENTES, A_MAIOR_Q_B, A_MENOR_Q_B);
  not not_1 (not_1_out, B[3]);
  not not_2 (not_2_out, B[3]);
  not not_3 (not_3_out, B[3]);
  not not_4 (not_4_out, B[3]);
  not not_5 (not_5_out, A[3]);
  not not_6 (not_6_out, A[3]);
  and and_3 (and_11_out[2], B_A[2], A_MENOR_Q_B, SB, not_7_out);
  not not_7 (not_7_out, A[3]);
  and and_4 (and_11_out[3], B_A[3], A_MENOR_Q_B, SB, not_8_out);
  not not_8 (not_8_out, A[3]);
  not not_9 (not_9_out, A[3]);
  not not_10 (not_10_out, A[3]);
  not not_11 (not_11_out, A[3]);
  not not_12 (not_12_out, A[3]);
  not not_13 (not_13_out, B[3]);
  not not_14 (not_14_out, B[3]);
  not not_15 (not_15_out, B[3]);
  and and_5 (and_17_out[3], B_A[3], A_MENOR_Q_B, SA, not_16_out);
  not not_16 (not_16_out, B[3]);
  and and_6 (and_6_out, A_MAIOR_Q_B, not_1_out, SA);
  and and_7 (and_7_out[0], A_B_t[0], A_MAIOR_Q_B, SA, not_1_out);
  and and_8 (and_7_out[1], A_B_t[1], A_MAIOR_Q_B, SA, not_2_out);
  and and_9 (and_7_out[2], A_B_t[2], A_MAIOR_Q_B, SA, not_3_out);
  and and_10 (and_7_out[3], A_B_t[3], A_MAIOR_Q_B, SA, not_4_out);
  and and_11 (and_11_out[0], B_A[0], A_MENOR_Q_B, SB, not_5_out);
  and and_12 (and_11_out[1], B_A[1], A_MENOR_Q_B, SB, not_6_out);
  and and_13 (and_13_out[0], A_B_t[0], A_MAIOR_Q_B, SB, not_9_out);
  and and_14 (and_13_out[1], A_B_t[1], A_MAIOR_Q_B, SB, not_10_out);
  and and_15 (and_13_out[2], A_B_t[2], A_MAIOR_Q_B, SB, not_11_out);
  and and_16 (and_13_out[3], A_B_t[3], A_MAIOR_Q_B, SB, not_12_out);
  and and_17 (and_17_out[0], B_A[0], A_MENOR_Q_B, SA, not_13_out);
  and and_18 (and_17_out[1], B_A[1], A_MENOR_Q_B, SA, not_14_out);
  and and_19 (and_17_out[2], B_A[2], A_MENOR_Q_B, SA, not_15_out);
  _7_Segment_Display u_7_segment_display_4 (.g(and_6_out));  // open: f, a, b, e, d, c, dp
  and and_20 (and_20_out, not_5_out, A_MENOR_Q_B, SB);
  _7_Segment_Display u_7_segment_display_5 (.g(and_20_out));  // open: f, a, b, e, d, c, dp
  _7_Segment_Display u_7_segment_display_6 (.e(and_13_out[0]));  // open: g, f, a, b, d, c, dp
  Hex_Digit_Display hex_digit_display_4 (.value(and_13_out));  // open: dp
  _7_Segment_Display u_7_segment_display_7 ();  // open: g, f, a, b, e, d, c, dp
  Hex_Digit_Display hex_digit_display_5 (.value(and_7_out));  // open: dp
  Hex_Digit_Display hex_digit_display_6 (.value(and_11_out));  // open: dp
  Hex_Digit_Display hex_digit_display_7 (.value(and_17_out));  // open: dp
  or or_2 (SINAL_SOMA, and_6_out, and_20_out, S_A_B_NEGATIVOS_E_DIFERENTES, SA_B_NEG__IGUAIS);
  assign DISPLAY_SOMA = A_B_POS_IGUAIS | A_B_NEG__IGUAIS | A_B_POS_EM_B_IGUAIS | A_B_POS_EM_A_IGUAIS | A_B_NEGATIVOS_E_DIFERENTES | A_B_POSITIVOS_E_DIFERENTES | and_7_out | and_11_out | and_13_out | and_17_out;  // OR_Gate or_3, 4 bits wide
  and and_21 (A_B_POSITIVOS_E_DIFERENTES[0], DIFERENTES, A_B[0], ~SA, ~SB);  // AND_Gate
  and and_22 (A_B_POSITIVOS_E_DIFERENTES[1], DIFERENTES, A_B[1], ~SA, ~SB);  // AND_Gate
  and and_23 (A_B_POSITIVOS_E_DIFERENTES[2], DIFERENTES, A_B[2], ~SA, ~SB);  // AND_Gate
  and and_24 (A_B_POSITIVOS_E_DIFERENTES[3], DIFERENTES, A_B[3], ~SA, ~SB);  // AND_Gate
  _7_Segment_Display u_7_segment_display_8 ();  // open: g, f, a, b, e, d, c, dp
  Hex_Digit_Display hex_digit_display_8 (.value(A_B_POSITIVOS_E_DIFERENTES));  // open: dp
  and and_25 (A_B_NEGATIVOS_E_DIFERENTES[0], DIFERENTES, A_B[0], SA, SB);
  and and_26 (A_B_NEGATIVOS_E_DIFERENTES[1], DIFERENTES, A_B[1], SA, SB);
  and and_27 (A_B_NEGATIVOS_E_DIFERENTES[2], DIFERENTES, A_B[2], SA, SB);
  and and_28 (A_B_NEGATIVOS_E_DIFERENTES[3], DIFERENTES, A_B[3], SA, SB);
  _7_Segment_Display u_7_segment_display_9 (.g(S_A_B_NEGATIVOS_E_DIFERENTES));  // open: f, a, b, e, d, c, dp
  and and_29 (S_A_B_NEGATIVOS_E_DIFERENTES, SA, DIFERENTES, SB);
  and and_30 (A_B_POS_EM_B_IGUAIS[0], A_PODE_SER_IGUAL_A_B, A_B_t[0], SA, ~SB);  // AND_Gate
  and and_31 (A_B_POS_EM_B_IGUAIS[1], A_PODE_SER_IGUAL_A_B, A_B_t[1], SA, ~SB);  // AND_Gate
  and and_32 (A_B_POS_EM_B_IGUAIS[2], A_PODE_SER_IGUAL_A_B, A_B_t[2], SA, ~SB);  // AND_Gate
  and and_33 (A_B_POS_EM_B_IGUAIS[3], A_PODE_SER_IGUAL_A_B, A_B_t[3], SA, ~SB);  // AND_Gate
  Hex_Digit_Display hex_digit_display_9 (.value(A_B_NEGATIVOS_E_DIFERENTES));  // open: dp
  and and_34 (A_B_POS_IGUAIS[0], A_PODE_SER_IGUAL_A_B, A_B[0], ~SA, ~SB);  // AND_Gate
  and and_35 (A_B_POS_IGUAIS[1], A_PODE_SER_IGUAL_A_B, A_B[1], ~SA, ~SB);  // AND_Gate
  and and_36 (A_B_POS_IGUAIS[2], A_PODE_SER_IGUAL_A_B, A_B[2], ~SA, ~SB);  // AND_Gate
  and and_37 (A_B_POS_IGUAIS[3], A_PODE_SER_IGUAL_A_B, A_B[3], ~SA, ~SB);  // AND_Gate
  _7_Segment_Display u_7_segment_display_10 ();  // open: g, f, a, b, e, d, c, dp
  _7_Segment_Display u_7_segment_display_11 ();  // open: g, f, a, b, e, d, c, dp
  Hex_Digit_Display hex_digit_display_10 (.value(A_B_POS_IGUAIS));  // open: dp
  Hex_Digit_Display hex_digit_display_11 (.value(A_B_POS_EM_B_IGUAIS));  // open: dp
  and and_38 (SA_B_NEG__IGUAIS, SA, A_PODE_SER_IGUAL_A_B, SB);
  _7_Segment_Display u_7_segment_display_12 (.g(SA_B_NEG__IGUAIS));  // open: f, a, b, e, d, c, dp
  and and_39 (A_B_NEG__IGUAIS[0], A_PODE_SER_IGUAL_A_B, A_B[0], SA, SB);
  and and_40 (A_B_NEG__IGUAIS[1], A_PODE_SER_IGUAL_A_B, A_B[1], SA, SB);
  and and_41 (A_B_NEG__IGUAIS[2], A_PODE_SER_IGUAL_A_B, A_B[2], SA, SB);
  and and_42 (A_B_NEG__IGUAIS[3], A_PODE_SER_IGUAL_A_B, A_B[3], SA, SB);
  Hex_Digit_Display hex_digit_display_12 (.value(A_B_NEG__IGUAIS));  // open: dp
  _7_Segment_Display u_7_segment_display_13 ();  // open: g, f, a, b, e, d, c, dp
  and and_43 (A_B_POS_EM_A_IGUAIS[0], A_PODE_SER_IGUAL_A_B, A_B_t[0], ~SA, SB);  // AND_Gate
  and and_44 (A_B_POS_EM_A_IGUAIS[1], A_PODE_SER_IGUAL_A_B, A_B_t[1], ~SA, SB);  // AND_Gate
  and and_45 (A_B_POS_EM_A_IGUAIS[2], A_PODE_SER_IGUAL_A_B, A_B_t[2], ~SA, SB);  // AND_Gate
  and and_46 (A_B_POS_EM_A_IGUAIS[3], A_PODE_SER_IGUAL_A_B, A_B_t[3], ~SA, SB);  // AND_Gate
  Hex_Digit_Display hex_digit_display_13 (.value(A_B_POS_EM_A_IGUAIS));  // open: dp

  // Other names for the same wires on the sheet: DISPLAY_SEMIFINAL[3:0] = DISPLAY_SOMA; SINAL_FINAL = SINAL_SOMA

  // Notes on the sheet:
  //   A > B E A < 0 E B > 0
  //   A < B E B < 0 E A > 0
  //   B3 = SB
  //   A > B E B < 0 E A > 0
  //   A < B E A < 0 E B > 0
endmodule

// Random emnúmeros do jogo
module \OF___Valor_aleatório_conv_para_valores_do_jogo  (
  input  Acertou,
  input  \PRÓXIMO ,
  input  RESET,
  input  Acertou_2,
  input  \PRÓXIMO_2 ,
  input  RESET_2,
  output [3:0] SAIDA_X,
  output SX,
  output [3:0] SAIDAy,
  output SY
);

  wire d_ff_1_q, d_ff_2_q, or_1_out, or_2_out;
  wire [3:0] Random_X_2_out, Random_X_out;

  D_Flip_Flop d_ff_1 (.Q(d_ff_1_q), .preset(Acertou), .reset(or_1_out));  // open: clk, D, Qn
  or or_1 (or_1_out, RESET, \PRÓXIMO );
  D_Flip_Flop d_ff_2 (.Q(d_ff_2_q), .preset(Acertou_2), .reset(or_2_out));  // open: clk, D, Qn
  or or_2 (or_2_out, RESET_2, \PRÓXIMO_2 );
  Random #(.width(4)) Random_X (.clk(\PRÓXIMO ), .next(d_ff_1_q), .out(Random_X_out), .clr(RESET));
  Random #(.width(4), .seed(1)) Random_X_2 (.clk(\PRÓXIMO_2 ), .next(d_ff_2_q), .out(Random_X_2_out), .clr(RESET_2));
  OF___Limitador_de_valores_p_pontuacao of_limitador_de_valores_p_pontuacao_1 (
    .\Saída (SAIDA_X), ._3(Random_X_out[3]), ._2(Random_X_out[2]), ._1(Random_X_out[1]),
    ._0(Random_X_out[0]), .out_6(SX));
  OF___Limitador_de_valores_p_pontuacao of_limitador_de_valores_p_pontuacao_2 (
    .\Saída (SAIDAy), ._3(Random_X_2_out[3]), ._2(Random_X_2_out[2]), ._1(Random_X_2_out[1]),
    ._0(Random_X_2_out[0]), .out_6(SY));
endmodule

module \OF___Peca_de_distribuição_organizada  (
  input  [3:0] VALOR,
  input  OUTRO,
  output _0,
  output _1,
  output _2,
  output _3
);

  and and_1 (_0, VALOR[0], OUTRO);
  and and_2 (_1, VALOR[1], OUTRO);
  and and_3 (_2, VALOR[2], OUTRO);
  and and_4 (_3, VALOR[3], OUTRO);
endmodule

module OF___Comparador (
  input  [3:0] P,
  input  [3:0] R,
  output Igual,
  output A__random___MENOR_que_B__meu,
  output A__random___MAIOR_que_B__meu
);

  Comparator comparator_1 ();  // open: a, b, gt, eq, lt
  // Igual igual_1: pin names not known; wires that end beside it: P, R, Igual
  // Maior maior_1: pin names not known; wires that end beside it: P, R, A__random___MAIOR_que_B__meu
  LED led_1 (.in(Igual));
  LED led_2 (.in(A__random___MENOR_que_B__meu));
  // Menor menor_1: pin names not known; wires that end beside it: Igual, A__random___MAIOR_que_B__meu, A__random___MENOR_que_B__meu
  LED led_3 (.in(A__random___MAIOR_que_B__meu));

  // Notes on the sheet:
  //   Player
  //   Random
  //   random menor maior ou igual ao do player
  //   Igual
  //   Menor
  //   Maior
endmodule

module OF___Incrementador_de_4_flipflops_normal (
  input  Botton,
  input  RESET,
  output [3:0] \SAÍDA_P__DISPLAY 
);

  wire [3:0] adder_1_out, d_ff_4_q;

  D_Flip_Flop d_ff_1 (.clk(Botton), .D(adder_1_out[3]), .Q(d_ff_4_q[3]), .reset(RESET));  // open: Qn, preset
  D_Flip_Flop d_ff_2 (.clk(Botton), .D(adder_1_out[2]), .Q(d_ff_4_q[2]), .reset(RESET));  // open: Qn, preset
  Adder #(.width(4)) adder_1 (.a(d_ff_4_q), .b(4'b0001), .out(adder_1_out));  // open: cin, cout
  D_Flip_Flop d_ff_3 (.clk(Botton), .D(adder_1_out[1]), .Q(d_ff_4_q[1]), .reset(RESET));  // open: Qn, preset
  D_Flip_Flop d_ff_4 (.clk(Botton), .D(adder_1_out[0]), .Q(d_ff_4_q[0]), .reset(RESET));  // open: Qn, preset
  Bit_Extender #(.in_width(4), .out_width(4), .\type ("zero")) bit_extender_1 (.in(d_ff_4_q), .out(\SAÍDA_P__DISPLAY ));
  Hex_Digit_Display hex_digit_display_1 (.value(\SAÍDA_P__DISPLAY ));  // open: dp
endmodule

module flipflop_estrutural (
  input  F1,
  input  F0,
  output Q
);

  wire and_1_out, and_2_out, and_3_out, and_4_out, not_1_out, not_3_out, not_4_out;

  buf and_1 (and_1_out, F1);  // AND_Gate
  buf and_2 (and_2_out, F0);  // AND_Gate
  not not_1 (not_1_out, and_1_out);
  not not_2 (Q, and_3_out);
  and and_3 (and_3_out, not_1_out, not_3_out);
  not not_3 (not_3_out, and_4_out);
  and and_4 (and_4_out, Q, not_4_out);
  not not_4 (not_4_out, and_2_out);
endmodule
